# Fritzing sketch Schematic Robot Car (saved by Fritzing 0.9.3b)
breadboards: 1

parts:
  Part1 = Arduino Uno (Rev3)
  VCC1 = Battery block 9V
  M1 = DC Motor
  M2 = DC Motor
  Part2 = Arduino Motor Shield
  hc-sr1 = hc-sr04

nets:
  N1: Part1.A0, hc-sr1.Trig
  N2: Part1.A1, hc-sr1.Echo
  N3: Part1.D4, Part2.A4
  N4: Part1.D5_PWM, Part2.A3
  N5: Part1.D6_PWM, Part2.A2
  N6: Part1.D7, Part2.A1
  5V: Part1.5V, hc-sr1.VCC
  GND: Part1.GND, VCC1.-, Part2.GND, hc-sr1.GND
  VIN: Part1.VIN, VCC1.+, Part2.5V
  N7: M1.pin_1, Part2.OUT1
  N8: M1.pin_2, Part2.OUT2
  N9: M2.pin_1, Part2.OUT3
  N10: M2.pin_2, Part2.OUT4

// code stored in the sketch: Untitled2.ino
int ;


void setup() {
  
}

void loop() {
// Turns on the LED if the ldrStatus is less than 700.
 

}
